# Fritzing sketch Esquema PCB ventilador (saved by Fritzing 0.9.2b)
circuit board: 3.8cm x 3cm
breadboards: 1

parts:
  M1 = DC Motor
  Q1 = NPN-Transistor [package="TO92 [THT]"]
  R1 = Resistor [tolerance=±5% resistance=220 package=THT]
  S1 = Pushbutton [package="[THT]"]
  R2 = Resistor [tolerance=±5% resistance=220 package=THT]
  D1 = Rectifier Diode [part_number=1N4001 package="300 mil [THT]"]

nets:
  N1: M1.pin_1, Q1.E, D1.cathode
  N2: M1.pin_2, D1.anode
  N3: Q1.B, R1.Pin_1
  N4: Q1.C, S1.Pin_3, S1.Pin_4
  N5: R1.Pin_0, S1.Pin_1, S1.Pin_2, R2.Pin_0
